# Fritzing sketch Garden_water (saved by Fritzing 0.9.3b)

parts:
  LED1 = RGB LED (com. cathode, rgb) [package="5 mm [THT]"]  # not connected
  Part1 = Arduino Mega 2560 (Rev3)
  part = ESP8266 WiFi Module [part_number=ESP8266]
  R1 = Resistor [tolerance=±5% resistance=220 package=THT]  # not connected
  R2 = Resistor [tolerance=±5% resistance=220 package=THT]  # not connected
  R3 = Resistor [tolerance=±5% resistance=220 package=THT]  # not connected
  DHT1 = DHT11 Humitidy and Temperature Sensor
  DHT2 = DHT11 Humitidy and Temperature Sensor
  WeMos_D1_Mini_Relay_Shield_V1 = WeMos D1 Mini Relay Shield V2
  WeMos_D1_Mini_Relay_Shield_V2 = WeMos D1 Mini Relay Shield V2
  WeMos_D1_Mini_Relay_Shield_V3 = WeMos D1 Mini Relay Shield V2
  Nokia_5110_LCD_Module1 = Nokia 5110 LCD  # not connected

nets:
  GND: Part1.GND, part.GND, DHT1.GND, DHT2.GND
  N1: Part1.D13_PWM, DHT1.DATA
  N2: Part1.D12_PWM, DHT2.DATA
  3V3: Part1.3V3, part.VCC, part.CH_PD
  VDD: Part1.5V, DHT1.VDD, DHT2.VDD
  N3: Part1.D3_PWM, WeMos_D1_Mini_Relay_Shield_V3.D1
  N4: Part1.D4_PWM, WeMos_D1_Mini_Relay_Shield_V2.D1
  N5: Part1.D5_PWM, WeMos_D1_Mini_Relay_Shield_V1.D1
  N6: Part1.D6_PWM, part.TXD
  N7: Part1.D7_PWM, part.RXD

notes:
  Rx -> Pin 7
  Tx -> Pin 6
  VCC - 3.3V
  GND
  Temp Out
  Temp In
  PUMP
  Mst Valve
  Outside Valve

custom parts:
  ESP8266 WiFi Module: Generic WiFi Module based on the ESP8266 with onboard PCB antenna and UART communications
  DHT11 Humitidy and Temperature Sensor: DHT11 Humidity and Temperature Sensor
  Nokia 5110 LCD: Nokia 5110 Graphic 84*48 LCD module such as the Sparkfun LCD-10168 or the clones from Ebay. There is example code for the Arduino available from the Sparkfun site in https://learn.sparkfun.com/tutorials/graphic-lcd-hookup-guide This is a 3.3V device, if you are running it from a 5V micro you need a 5V tolorant level translator such as the 74ahc367 to protect the signal imputs. Rafa G. did a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
